# Fritzing sketch Deskpet (saved by Fritzing 0.9.9b)
breadboards: 1

parts:
  Composant1 = Arduino Nano (Rev3.0)
  OLED_I2C1 = OLED 128x64 I2C Monochrome Display
  HC-SR04_Sensor_1 = HC-SR04 Ultrasonic Distance Sensor
  J1 = Piezo Speaker
  S1 = Pushbutton [package="[THT]"]
  S2 = Pushbutton [package="[THT]"]
  S3 = Pushbutton [package="[THT]"]
  S4 = Pushbutton [package="[THT]"]

nets:
  GND: Composant1.GND, OLED_I2C1.GND, HC-SR04_Sensor_1.GND, J1.pin1, S1.Pin_3, S1.Pin_4, S2.Pin_3, S2.Pin_4, S3.Pin_3, S3.Pin_4, S4.Pin_3, S4.Pin_4
  N1: Composant1.D5, J1.pin2
  N2: Composant1.D7, S1.Pin_1, S1.Pin_2
  N3: Composant1.D8, S2.Pin_1, S2.Pin_2
  N4: Composant1.D9, S3.Pin_1, S3.Pin_2
  N5: Composant1.D10, S4.Pin_1, S4.Pin_2
  N6: Composant1.D11/MOSI, HC-SR04_Sensor_1.ECHO
  N7: Composant1.D12/MISO, HC-SR04_Sensor_1.TRIG
  5V: Composant1.5V, OLED_I2C1.VDD, HC-SR04_Sensor_1.VCC
  N8: Composant1.A5, OLED_I2C1.SCK
  N9: Composant1.A4, OLED_I2C1.SDA
